// Logisim project Adder.circ as structural Verilog: 1 circuit, main circuit main
module main (
  input  in_1,
  input  in_2,
  input  in_3,
  input  in_4,
  output out_5,
  output out_6
);

  wire and_1_out, and_2_out, and_3_out, and_4_out, undriven, xor_1_out, xor_3_out;

  and and_1 (and_1_out, in_1, in_2);
  xor xor_1 (xor_1_out, in_1, in_2);
  and and_2 (and_2_out, xor_1_out, in_3);
  xor xor_2 (out_6, in_3, xor_1_out);
  // AND_Gate and_3 has open pins: out=and_3_out
  // XOR_Gate xor_3 has open pins: out=xor_3_out
  or or_1 (out_5, and_1_out, and_2_out);
  and and_4 (and_4_out, xor_3_out, undriven);
  // XOR_Gate xor_4 has open pins: in0=undriven, in1=xor_3_out, out=open
  // OR_Gate or_2 has open pins: in2=and_3_out, in3=and_4_out, out=open
endmodule
